# Fritzing sketch Alles (saved by Fritzing 0.9.2b)
breadboards: 1

parts:
  Arduino = Arduino Uno (Rev3)
  LCD-Display = LCD screen
  Kontrast-Poti = Rotary Potentiometer (Small) [maximum_resistance=10kΩ package=THT]
  Vorwiderstand = Resistor [tolerance=±5% resistance=220 package=THT]
  LM35 = LM35 Temperature Sensor [package="TO92 [THT]"]
  DHT11 = Humidity and Temperature Sensor RHT03
  S1 = Toggle Switch [package=THT]
  Batterie_1 = Battery
  Batterie_2 = Battery
  Kondensator = Electrolytic Capacitor [capacitance=5µF voltage=16V package="100 mil [THT, electrolytic]"]
  Zenerdiode = Zener Diode [part_number=1N4732A breakdown_voltage=12V package="300 mil [THT]"]
  An/Aus_Schalter = Pushbutton [package=THT]
  Netzteil = DC Power [voltage=12V]

nets:
  N1: Arduino.A0, LM35.Vout
  N2: Arduino.D8, LCD-Display.E
  N3: Arduino.D9_PWM, LCD-Display.RS
  Wifi-Shield SS: Arduino.D10_PWM/SS
  Wifi-Shield MOSI: Arduino.D11_PWM/MOSI
  Wifi-Shield MISO: Arduino.D12/MISO
  Wifi-Shield SCK: Arduino.D13/SCK
  GND: Arduino.GND, LCD-Display.VSS, LCD-Display.R/W, LCD-Display.LED-, Kontrast-Poti.leg1, LM35.GND, DHT11.GND_2, Batterie_2.-, Kondensator.-, Zenerdiode.cathode, Netzteil.V-
  N4: Arduino.D2, LCD-Display.DB7
  N5: Arduino.D3_PWM, LCD-Display.DB6
  N6: Arduino.D4, LCD-Display.DB5
  N7: Arduino.D5_PWM, LCD-Display.DB4
  N8: Arduino.D6_PWM, DHT11.Data-signal
  Wifi-Shield Handshake: Arduino.D7
  5V: Arduino.5V, LCD-Display.VDD, Kontrast-Poti.leg2, Vorwiderstand.Pin_0, LM35.+Vs, DHT11.Vcc
  N9: Arduino.VIN, An/Aus_Schalter.leg0
  N10: LCD-Display.V0, Kontrast-Poti.wiper
  N11: LCD-Display.LED+, Vorwiderstand.Pin_1
  N12: S1.L1, Netzteil.V+
  N13: S1.COM, Kondensator.+, Zenerdiode.anode, An/Aus_Schalter.leg1
  N14: S1.L2, Batterie_1.+
  N15: Batterie_1.-, Batterie_2.+
