# Fritzing sketch LCD-Display (saved by Fritzing 0.9.2b)
breadboards: 1

parts:
  Arduino = Arduino Uno (Rev3)
  LCD-Display = LCD screen
  R1 = Rotary Potentiometer (Small) [maximum_resistance=10kΩ package=THT]
  R2 = Resistor [tolerance=±5% resistance=220 package=THT]

nets:
  N1: Arduino.D11_PWM/MOSI, LCD-Display.E
  N2: Arduino.D12/MISO, LCD-Display.RS
  GND: Arduino.GND, LCD-Display.VSS, LCD-Display.R/W, LCD-Display.LED-, R1.leg1
  N3: Arduino.D2, LCD-Display.DB7
  N4: Arduino.D3_PWM, LCD-Display.DB6
  N5: Arduino.D4, LCD-Display.DB5
  N6: Arduino.D5_PWM, LCD-Display.DB4
  5V: Arduino.5V, LCD-Display.VDD, R1.leg2, R2.Pin_0
  N7: LCD-Display.V0, R1.wiper
  N8: LCD-Display.LED+, R2.Pin_1
